# Fritzing sketch Circuit Diagram (saved by Fritzing 1.0.6)

parts:
  S1 = H-Bridge with L298N
  M1 = Getriebemotor
  M2 = Getriebemotor
  M3 = Getriebemotor
  M4 = Getriebemotor
  U1 = ESP32S-HiLetgo [part_number=ESP32S-HiLetgo]
  BAT1 = 18650 battery holder [package=battery-18650-kit]
  BAT2 = 18650 battery holder [package=battery-18650-kit]
  BAT3 = 18650 battery holder [package=battery-18650-kit]
  HC-SR04_FRONT_1 = HC-SR04 Ultrasonic Distance Sensor
  HC-SR04_FRONT_2 = HC-SR04 Ultrasonic Distance Sensor
  SEN0019_RIGHT = DF Robot IR (SEN0019)
  SEN0019_LEFT = DF Robot IR (SEN0019)
  KY-033_BACK_LEFT = KY-033 Tracing Black White Line Hunting Sensor Module For Arduino
  KY-033_BACK_RIGHT = KY-033 Tracing Black White Line Hunting Sensor Module For Arduino
  KY-033_FRONT_LEFT = KY-033 Tracing Black White Line Hunting Sensor Module For Arduino
  KY-033_FRONT_RIGHT = KY-033 Tracing Black White Line Hunting Sensor Module For Arduino
  U3 = CR-3050B 5V converter [package=dc-dc_converter]

nets:
  12V: S1.12V, BAT3.+, U3.VIN
  N1: S1.GND, BAT1.-, U3.GND#1
  N2: S1.M1-01, M1.pin_2, M4.pin_2
  N3: S1.M1-02, M1.pin_1, M4.pin_1
  N4: S1.M2-01, M2.pin_1, M3.pin_2
  N5: S1.M2-02, M2.pin_2, M3.pin_1
  N6: U1.GPIO34, SEN0019_LEFT.SIGNAL
  N7: U1.GPIO35, SEN0019_RIGHT.SIGNAL
  N8: U1.GPIO32, KY-033_FRONT_RIGHT.S
  N9: U1.GPIO33, KY-033_FRONT_LEFT.S
  GND: U1.GPIO9, HC-SR04_FRONT_1.GND, HC-SR04_FRONT_2.GND, SEN0019_RIGHT.GND, SEN0019_LEFT.GND, KY-033_BACK_LEFT.GND, KY-033_BACK_RIGHT.GND, KY-033_FRONT_LEFT.GND, KY-033_FRONT_RIGHT.GND, U3.GND#2
  VCC: U1.VIN, HC-SR04_FRONT_1.VCC, HC-SR04_FRONT_2.VCC, SEN0019_RIGHT.VCC, SEN0019_LEFT.VCC, KY-033_BACK_LEFT.V+, KY-033_BACK_RIGHT.V+, KY-033_FRONT_LEFT.V+, KY-033_FRONT_RIGHT.V+, U3.VOUT
  N10: U1.GPIO4, HC-SR04_FRONT_1.TRIG
  N11: U1.GPIO16, HC-SR04_FRONT_1.ECHO
  N12: U1.GPIO17, HC-SR04_FRONT_2.ECHO
  N13: U1.GPIO5, HC-SR04_FRONT_2.TRIG
  N14: U1.GPIO21, KY-033_BACK_LEFT.S
  N15: U1.GPIO22, KY-033_BACK_RIGHT.S
  N16: BAT1.+, BAT2.+
  N17: BAT2.-, BAT3.-

custom parts:
  H-Bridge with L298N: h-bridge
  ESP32S-HiLetgo: HiLetgo ESP-WROOM-32 ESP32 ESP-32S Development Board 2.4GHz Dual-Mode WiFi + Bluetooth Dual Cores Microcontroller The ESP32 integrated with Antenna switches, RF Balun, power amplifiers, low-noise amplifiers, filters, and management modules, and the entire solution occupies the least area of PCB. 2.4 GHz Wi-Fi plus Bluetooth dual-mode chip, with TSMC Ultra-low power consumption 40nm technology,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
  18650 battery holder: 18650 Battery Holder
  KY-033 Tracing Black White Line Hunting Sensor Module For Arduino: Tracing Black White Line Hunting Sensor Module For Arduino Description: This is KY-033 tracking sensor. The KY-033 measures the intensity of infrared radiation and delivers it as an analog output voltage. Features: Operating voltage: 2.5 - 12V(cannot over12V) working current: 18mA-20mA at 5V Enhanced accuracy Documents: http://www.vishay.com/docs/83760/tcrt5000.pdf
  CR-3050B 5V converter: CR-3050B 5-36V to 5V converter
